// Logisim project char.circ as structural Verilog: 1 circuit, main circuit main
module main (
);

  wire Clock_out, n27245_1_b0, n27245_1_b1, n27245_1_b2, n27245_1_b3, n27245_1_b4, n27245_1_b5, n27245_1_b6,
       n27245_1_b7, n74273_1_p12, n74273_1_p13, n74273_1_p14, n74273_1_p15, n74273_1_p16, n74273_1_p17,
       n74273_1_p18, n74273_1_p19;

  Clock Clock (.out(Clock_out));
  _27245 u_27245_1 (
    .DIR(1'b1), .A0(1'b0), .A1(1'b0), .A2(1'b0), .A3(1'b0), .A4(1'b0), .A5(1'b0), .A6(1'b1), .A7(1'b1),
    .B0(n27245_1_b0), .B1(n27245_1_b1), .B2(n27245_1_b2), .B3(n27245_1_b3), .B4(n27245_1_b4),
    .B5(n27245_1_b5), .B6(n27245_1_b6), .B7(n27245_1_b7), .ENABLE(1'b0));
  // _74273 74273_1: pin names not known; wires that end beside it: 1'b0, n27245_1_b0, n27245_1_b1, n27245_1_b2, n27245_1_b3, n27245_1_b4, n27245_1_b5, n27245_1_b6, n27245_1_b7, 1'b1, Clock_out, n74273_1_p12, n74273_1_p13, n74273_1_p14, n74273_1_p15, n74273_1_p16, n74273_1_p17, n74273_1_p18, n74273_1_p19
  LED led_1 (.in(n74273_1_p12));
  LED led_2 (.in(n74273_1_p13));
  LED led_3 (.in(n74273_1_p14));
  LED led_4 (.in(n74273_1_p15));
  LED led_5 (.in(n74273_1_p16));
  LED led_6 (.in(n74273_1_p17));
  LED led_7 (.in(n74273_1_p18));
  LED led_8 (.in(n74273_1_p19));

  // Notes on the sheet:
  //   Power
  //   Data Bus
endmodule
